# Fritzing sketch AC&C._20180622 (saved by Fritzing 0.9.3b)
breadboards: 1

parts:
  R2 = Resistor [tolerance=±5% resistance=220 package=THT]
  R3 = Resistor [tolerance=±5% resistance=220 package=THT]
  F1 = Fan - Ventilador [package=THT]
  KY-1 = Keyes Relay [package=THT]
  Part1 = KY-015 Temperature & Humidity Sensor Module [package="Breakout board"]
  WeMos_D1_R1 = WeMos D1 R2
  VCC2 = 4 x AAA Battery Mount
  LED1 = RGB LED (com. cathode, rgb) [package="5 mm [THT]"]
  R1 = Resistor [tolerance=±5% resistance=220 package=THT]
  U1 = Sharp Dust Sensor [part_number=GP2Y1010AU0F]

nets:
  N1: R2.Pin_0, LED1.red_anode
  N2: R2.Pin_1, WeMos_D1_R1.(D5)
  N3: R3.Pin_0, WeMos_D1_R1.(D6)
  N4: R3.Pin_1, LED1.green_anode
  N5: F1.5V, KY-1.NO
  N6: F1.GND, VCC2.-
  N7: KY-1.signal, WeMos_D1_R1.D2
  VIN: KY-1.power, Part1.Vin, WeMos_D1_R1.5V, U1.Vo
  N8: KY-1.ground, Part1.-, WeMos_D1_R1.GND, U1.S-GND
  N9: KY-1.C, VCC2.+
  N10: Part1.S, WeMos_D1_R1.D3
  N11: WeMos_D1_R1.D0/RX, U1.LED
  N12: WeMos_D1_R1.D1/TX, U1.LED-GND
  N13: WeMos_D1_R1.(D7), R1.Pin_0
  N14: LED1.blue_anode, R1.Pin_1

custom parts:
  Fan - Ventilador: Ventilador de 2 pines, se encuentra comunmente en computadoras de escritorio
  Keyes Relay: The Keyes 5V relay module is suitable for SCM development, home appliance control. It uses a 5V~12V TIL control signal which can control DC / AC signal.
  KY-015 Temperature & Humidity Sensor Module: KY-015 temperature and humidity sensor module, provides a low-latency serial interface to measure humidity and temperature.
  WeMos D1 R2: The D1 R2 is a mini wifi board based on the ESP-8266EX.
  Sharp Dust Sensor: Sharp GP2Y1010AU0F Dust Sensor
