# Fritzing sketch AC&C_20180622 (saved by Fritzing 0.9.3b)
breadboards: 1

parts:
  WeMos_D1_R1 = WeMos D1 R2
  부품1 = LCD1602-I2C
  BT1 = Bluetooth HC-06u [package=THT]
  부품2 = Adafruit 1.44 inch TFT Breakout [part_number="Adafruit #2088"]

nets:
  N1: WeMos_D1_R1.D0/RX, BT1.TXD
  N2: WeMos_D1_R1.D1/TX, BT1.RXD
  N3: WeMos_D1_R1.D3, 부품1.SCL
  N4: WeMos_D1_R1.D4, 부품1.SDA
  N5: WeMos_D1_R1.D8, 부품2.SCK
  N6: WeMos_D1_R1.D9, 부품2.MISO
  N7: WeMos_D1_R1.D10, 부품2.MOSI
  N8: WeMos_D1_R1.D11, 부품2.GND
  N9: WeMos_D1_R1.D13, 부품2.+3V3
  N10: WeMos_D1_R1.GND#20, 부품1.GND
  N11: WeMos_D1_R1.GND#21, BT1.GND, 부품2.TFTCS
  5V: WeMos_D1_R1.5V, 부품1.VCC, 부품2.LED
  3.3V: WeMos_D1_R1.3.3V, BT1.VCC

custom parts:
  WeMos D1 R2: The D1 R2 is a mini wifi board based on the ESP-8266EX.
  LCD1602-I2C: A standard character display, usually with 2x16 characters. Comes in many colors with LCM1602 IIC attached.
  Bluetooth HC-06u: Bluetooth HC-06 - face up, pins down 16.5mm x 37.5mm PCB
  Adafruit 1.44 inch TFT Breakout: This lovely little display breakout is the best way to add a small, colorful and bright display to any project. Since the display uses 4-wire SPI to communicate and has its own pixel-addressable frame buffer, it can be used with every kind of microcontroller. Even a very small one with low memory and few pins available! The 1.44" display has 128x128 color pixels. Unlike the low cost "Nokia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
